# Fritzing sketch pcb (saved by Fritzing 0.8.7b)
circuit board: 13.5328cm x 7.41572cm
breadboards: 2

parts:
  U1 = Voltage Regulator - 5V [package="TO220 [THT]"]
  C1 = Electrolytic Capacitor [capacitance=100µF package="200 mil [THT, electrolytic]"]
  C2 = Capacitor [package=cap-pth-small2]
  R1 = Resistor [tolerance=±5% resistance=220 package=THT]
  L293D = L293D [package=THT]
  M1 = DC Motor
  J2 = Screw terminal - 2 pins [package=THT]
  M2 = DC Motor
  D1 = Diode [package=diode-1n4148]
  VCC1 = Battery block 9V
  J1 = Screw terminal - 2 pins [package=THT]
  S1 = Pushbutton [package=THT]
  PICO_W = Raspberry Pi Pico W

nets:
  N1: U1.input_voltage, L293D.+Vmotor, S1.leg0
  N2: U1.GND, L293D.0V, VCC1.-, PICO_W.pin_3, PICO_W.pin_8, PICO_W.pin_13, PICO_W.pin_18, PICO_W.pin_23, PICO_W.pin_28, PICO_W.pin_33, PICO_W.pin_38
  N3: U1.output_voltage, C1.-, C2.1, R1.Pin_0, L293D.+V, D1.C
  N4: C1.+, C2.2, R1.Pin_1
  N5: L293D.Enable_1, PICO_W.pin_7
  N6: L293D.In_1, PICO_W.pin_10
  N7: L293D.Out_1_(_Controlled_by_Enable_1_), M1.pin_1, J1.pin2
  N8: L293D.Out_2_(_Controlled_by_Enable_1_), M1.pin_2, J1.pin1
  N9: L293D.In_2, PICO_W.pin_11
  N10: L293D.Enable_2, PICO_W.pin_27
  N11: L293D.In_3, PICO_W.pin_26
  N12: L293D.Out_3_(_Controlled_by_Enable_2_), J2.pin2, M2.pin_1
  N13: L293D.Out_4_(_Controlled_by_Enable_2_), J2.pin1, M2.pin_2
  N14: L293D.In_4, PICO_W.pin_34
  N15: D1.A, PICO_W.pin_39
  N16: VCC1.+, S1.leg1

custom parts:
  Raspberry Pi Pico W: Raspberry Pi Pico W. Based around the RP2040 microcontroller the Pico W is a low cost microcontroller device bringing Raspberry Pi quality, cost, and easy of use to the microcontroller space. The areas marked KEEPOUT in pcb silkscreen should not have traces running through them to avoid shorts on a soldered in module!
